// Logisim project D1-1-2 XNOR.circ as structural Verilog: 1 circuit, main circuit main
module main (
  input  A,
  input  B,
  input  C,
  output OUT
);

  wire xnor_1_out, xnor_2_out, xnor_3_out;

  xnor xnor_1 (xnor_1_out, B, A);
  xnor xnor_2 (xnor_2_out, A, C);
  xnor xnor_3 (xnor_3_out, C, B);
  and and_1 (OUT, xnor_1_out, xnor_2_out);
  and and_2 (OUT, xnor_2_out, xnor_3_out);
endmodule
