// Logisim project D1-2-1 HA.circ as structural Verilog: 1 circuit, main circuit main
module main (
  input  A,
  input  B,
  output SUM,
  output COUT
);

  xor xor_1 (SUM, A, B);
  and and_1 (COUT, B, A);
endmodule
