// Logisim project D1-2-2 FA.circ as structural Verilog: 3 circuits, main circuit 手绘全加器
module \半加器自动生成  (
  input  A,
  input  B,
  output Co,
  output S
);
endmodule

// FA
module \手绘全加器  (
  input  Ai,
  input  Bi,
  input  Cin,
  output Si,
  output Cout
);

  wire and_1_out, and_2_out, and_3_out, xor_1_out;

  and and_1 (and_1_out, Ai, Bi);
  and and_2 (and_2_out, Ai, Cin);
  and and_3 (and_3_out, Bi, Cin);
  xor xor_1 (xor_1_out, Ai, Bi);
  or or_1 (Cout, and_1_out, and_2_out, and_3_out);
  xor xor_2 (Si, xor_1_out, Cin);

  // Other names for the same wires on the sheet: Ci = Cin; Co = Cout

  // Notes on the sheet:
  //   输入引脚
  //   请勿增加、删除引脚，用隧道标签构建电路
  //   注意不要使用“组合逻辑分析”工具自动生成电路，自动生成会改变电路配置和封装外观！
  //   输出引脚
  //   请勿更改电路封装外观
endmodule

// 4位加法
module \_4位行波进位加法器  (
  input  [3:0] X,
  input  [3:0] Y,
  input  Cin,
  output [3:0] Sum,
  output Cout
);

  // Probe on X
  // Probe on Y
  // Probe on Sum
  // Probe on X
  // Probe on Y
  // Probe on Sum

  // Other names for the same wires on the sheet: Ci = Cin; Co = Cout; S[3:0] = Sum; S0 = Sum[0]; S1 = Sum[1];
  //   S2 = Sum[2]; S3 = Sum[3]

  // Notes on the sheet:
  //   Cin: pull=down
  //   X: pull=down
  //   Y: pull=down
  //   输入引脚区
  //   输出引脚区
  //   功能说明:4位串行加法器 S=X+Y+Cin，Cout为最高位进位，Cin为进位输入
  //   +
  //   =
  //   有符号加法
  //   +
  //   =
  //   无符号加法
endmodule
