// Logisim project D1-2-3 4Bit FA.circ as structural Verilog: 2 circuits, main circuit main
module main (
  input  Y3,
  input  X3,
  input  Y2,
  input  X2,
  input  Y1,
  input  X1,
  input  Y0,
  input  X0,
  input  C0,
  output C4,
  output S4,
  output S2,
  output S1,
  output S0
);

  wire fa_2_out_5, fa_3_out_5, fa_4_out_5;

  FA fa_1 (.in_1(X3), .in_2(Y3), .in_3(fa_2_out_5), .out_4(S4), .out_5(C4));
  FA fa_2 (.in_1(X2), .in_2(Y2), .in_3(fa_3_out_5), .out_4(S2), .out_5(fa_2_out_5));
  FA fa_3 (.in_1(X1), .in_2(Y1), .in_3(fa_4_out_5), .out_4(S1), .out_5(fa_3_out_5));
  FA fa_4 (.in_1(X0), .in_2(Y0), .in_3(C0), .out_4(S0), .out_5(fa_4_out_5));
endmodule

module FA (
  input  in_1,
  input  in_2,
  input  in_3,
  output out_4,
  output out_5
);

  wire and_1_out, and_2_out, and_3_out, xor_1_out;

  xor xor_1 (xor_1_out, in_1, in_2);
  and and_1 (and_1_out, in_1, in_2);
  and and_2 (and_2_out, in_1, in_3);
  and and_3 (and_3_out, in_2, in_3);
  xor xor_2 (out_4, xor_1_out, in_3);
  or or_1 (out_5, and_1_out, and_2_out, and_3_out);
endmodule
