// Logisim project D1-2-4 CMP.circ as structural Verilog: 3 circuits, main circuit 2位比较器
module \_1位比较器  (
  input  X,
  input  Y,
  output Great,
  output Equal,
  output Less
);

  wire not_1_out;

  not not_1 (not_1_out, Y);
  xnor xnor_1 (Equal, X, Y);
  and and_1 (Great, not_1_out, X);
  nor nor_1 (Less, Equal, Great);

  // Notes on the sheet:
  //   电路功能：X,Y进行比较，Great=(X>Y)?1:0;
  //   输入引脚区
  //   输出引脚区
endmodule

module \_2位比较器  (
  input  [1:0] X,
  input  [1:0] Y,
  output Great,
  output Equal,
  output Less
);

  wire and_1_out, and_3_out, \n1位比较器_1_equal , \n1位比较器_1_great , \n1位比较器_1_less , \n1位比较器_2_equal ,
       \n1位比较器_2_great , \n1位比较器_2_less ;

  // Probe on X
  // Probe on Y
  \_1位比较器  \u_1位比较器_1  (.X(X[1]), .Y(Y[1]), .Great(\n1位比较器_1_great ), .Equal(\n1位比较器_1_equal ), .Less(\n1位比较器_1_less ));
  \_1位比较器  \u_1位比较器_2  (.X(X[0]), .Y(Y[0]), .Great(\n1位比较器_2_great ), .Equal(\n1位比较器_2_equal ), .Less(\n1位比较器_2_less ));
  and and_1 (and_1_out, \n1位比较器_1_equal , \n1位比较器_2_great );
  and and_2 (Equal, \n1位比较器_1_equal , \n1位比较器_2_equal );
  and and_3 (and_3_out, \n1位比较器_2_less , \n1位比较器_1_equal );
  or or_1 (Great, \n1位比较器_1_great , and_1_out);
  or or_2 (Less, and_3_out, \n1位比较器_1_less );

  // Notes on the sheet:
  //   电路功能：X,Y进行无符号比较，Great=(X>Y)?1:0;
  //   输入引脚区
  //   输出引脚区
endmodule

// 4位比较
module \_4位无符号比较器  (
  input  [3:0] X,
  input  [3:0] Y,
  output Great,
  output Equal,
  output Less
);

  wire and_2_out, and_3_out, \n2位比较器_1_equal , \n2位比较器_1_great , \n2位比较器_1_less , \n2位比较器_2_equal ,
       \n2位比较器_2_great , \n2位比较器_2_less ;

  \_2位比较器  \u_2位比较器_1  (
    .X(X[3:2]), .Y(Y[3:2]), .Great(\n2位比较器_1_great ), .Equal(\n2位比较器_1_equal ), .Less(\n2位比较器_1_less ));
  \_2位比较器  \u_2位比较器_2  (
    .X(X[1:0]), .Y(Y[1:0]), .Great(\n2位比较器_2_great ), .Equal(\n2位比较器_2_equal ), .Less(\n2位比较器_2_less ));
  // Probe on X
  // Probe on Y
  and and_1 (Equal, \n2位比较器_1_equal , \n2位比较器_2_equal );
  and and_2 (and_2_out, \n2位比较器_2_less , \n2位比较器_1_equal );
  and and_3 (and_3_out, \n2位比较器_1_equal , \n2位比较器_2_great );
  or or_1 (Less, \n2位比较器_1_less , and_2_out);
  or or_2 (Great, \n2位比较器_1_great , and_3_out);

  // Notes on the sheet:
  //   电路功能：X,Y进行无符号比较，Great=(X>Y)?1:0;
  //   输入引脚区
  //   输出引脚区
endmodule
