// Logisim project D1-2-6 MUX.circ as structural Verilog: 4 circuits, main circuit 2选1MUX
// MUX2-1
module \_2选1MUX  (
  input  D0,
  input  Select,
  input  D1,
  input  nEnable,
  output F
);

  wire and_1_out, and_2_out, not_1_out, or_1_out;

  and and_1 (and_1_out, D0, not_1_out);
  not not_1 (not_1_out, Select);
  and and_2 (and_2_out, Select, D1);
  or or_1 (or_1_out, and_1_out, and_2_out);
  or or_2 (F, nEnable, or_1_out);

  // Notes on the sheet:
  //   nEnable: pull=down
  //   2选1数据选择器，使能信号nEnable低电平有效
  //   请不要改变封装外观！
endmodule

// MUX4-1
module \_4选1MUX  (
  input  D0,
  input  D2,
  input  [1:0] Select,
  input  D1,
  input  D3,
  input  nEnable,
  output F
);

  wire \n2选1mux_1_f , \n2选1mux_2_f ;

  \_2选1MUX  \u_2选1mux_1  (.D0(D0), .Select(Select[0]), .F(\n2选1mux_1_f ), .D1(D1), .nEnable(nEnable));
  \_2选1MUX  \u_2选1mux_2  (.D0(D2), .Select(Select[0]), .F(\n2选1mux_2_f ), .D1(D3), .nEnable(nEnable));
  \_2选1MUX  \u_2选1mux_3  (.D0(\n2选1mux_1_f ), .Select(Select[1]), .F(F), .D1(\n2选1mux_2_f ), .nEnable(nEnable));

  // Notes on the sheet:
  //   nEnable: pull=down
  //   4选1数据选择器，使能信号nEnable低电平有效
  //   请不要改变封装外观！
endmodule

// MUX8-1
module \_8选1MUX  (
  input  D0,
  input  D4,
  input  [2:0] Select,
  input  D1,
  input  D5,
  input  nEnable,
  input  D2,
  input  D6,
  input  D3,
  input  D7,
  output F
);

  wire \n4选1mux_1_f , \n4选1mux_2_f ;

  \_4选1MUX  \u_4选1mux_1  (
    .D0(D0), .D2(D2), .Select(Select[1:0]), .F(\n4选1mux_1_f ), .D1(D1), .D3(D3), .nEnable(nEnable));
  \_4选1MUX  \u_4选1mux_2  (
    .D0(D4), .D2(D6), .Select(Select[1:0]), .F(\n4选1mux_2_f ), .D1(D5), .D3(D7), .nEnable(nEnable));
  \_2选1MUX  \u_2选1mux_1  (.D0(\n4选1mux_1_f ), .Select(Select[2]), .F(F), .D1(\n4选1mux_2_f ), .nEnable(nEnable));

  // Notes on the sheet:
  //   nEnable: pull=down
  //   8选1数据选择器，使能信号nEnable低电平有效
  //   请不要改变封装外观！
endmodule

module \MUX应用  (
  input  A,
  input  B,
  input  nEnable,
  input  Ci,
  output Sum,
  output Co
);

  wire not_1_out;

  not not_1 (not_1_out, Ci);
  \_4选1MUX  \u_4选1mux_1  (
    .D0(Ci), .D2(not_1_out), .Select({A, B}), .F(Sum), .D1(not_1_out), .D3(Ci), .nEnable(nEnable));
  \_4选1MUX  \u_4选1mux_2  (.D0(1'b0), .D2(Ci), .Select({A, B}), .F(Co), .D1(Ci), .D3(1'b1), .nEnable(nEnable));

  // Notes on the sheet:
  //   nEnable: pull=down
  //   使用8选1或者4选1数据选择器构建全加器FA
  //   请不要改变封装外观！
endmodule
