// Logisim project D1-3-1 RS.circ as structural Verilog: 1 circuit, main circuit main
module main (
  input  R,
  input  S,
  output Qa,
  output Qb
);

  nor nor_1 (Qa, R, Qb);
  nor nor_2 (Qb, Qa, S);
endmodule
