// Logisim project D1-3-2 Clocked RS.circ as structural Verilog: 1 circuit, main circuit main
module main (
  input  R,
  input  CLK,
  input  S,
  output Q,
  output nQ
);

  wire and_1_out, and_2_out;

  and and_1 (and_1_out, R, CLK);
  and and_2 (and_2_out, CLK, S);
  S_R_Flip_Flop s_r_ff_1 (.S(and_1_out), .R(and_2_out), .Q(Q), .Qn(nQ));  // open: clk, preset, reset, en
endmodule
